// Logisim project module.circ as structural Verilog: 9 circuits, main circuit main
module main (
);

  wire ds1302_1_gnd, rotaryencoder_1_gnd, speaker_1_gnd, stepupmodule_1_vcc_5v, tp4056_1_b_gnd,
       tp4056_1_b_vcc, tp4056_1_out_gnd, tp4056_1_out_vcc, undriven, undriven_2, undriven_3, undriven_4,
       undriven_5, undriven_6, undriven_7, undriven_8, undriven_9, undriven_10, undriven_11, undriven_12;

  Speaker speaker_1 (.Vcc(undriven), .GND(speaker_1_gnd));
  NodeMCUv2 nodemcuv2_1 (
    .SD3(undriven), .GND_1(speaker_1_gnd), .GND_2(tp4056_1_out_gnd), .Vin(tp4056_1_out_vcc), .D0(undriven_8),
    .D1(undriven_5), .D2(undriven_9), .D3(undriven_7), .Vout_3V3_2(undriven_6), .GND_3(ds1302_1_gnd),
    .D5(undriven_10), .D6(undriven_11), .D7(undriven_12), .D8(undriven_2), .D9(undriven_3), .D10(undriven_4));  // open: A0, RSV_1, RSV_2, SD2, SD1, CMD, SD0, CLK, Vout_3V3_1, EN, RST, D4, GND_4, Vout_3V3_3
  TP4056 tp4056_1 (
    .B_Vcc(tp4056_1_b_vcc), .B_GND(tp4056_1_b_gnd), .Out_GND(tp4056_1_out_gnd), .Out_Vcc(tp4056_1_out_vcc));  // open: IN_GND, IN_Vcc
  Battery battery_1 (.B_in(tp4056_1_b_vcc), .B_out(tp4056_1_b_gnd));
  MRB3503 mrb3503_1 (
    .GND_1(ds1302_1_gnd), .RS(undriven_9), .Vcc_2(undriven_6), .CS(undriven_8), .WR(undriven_5),
    .RST(undriven_7));  // open: DB4, DB6, DB8, DB10, DB12, DB14, SDCS, Vcc_1, Vout_5V, MOSI, F_CS, CLK, RD, DB0, DB2, DB3, DB5, DB7, DB9, DB11, DB13, DB15, BL, GND_2, MISO, PEN, T_CS, DB1
  DS1302 ds1302_1 (.Vcc(undriven_6), .CLK(undriven_2), .DAT(undriven_3), .RST(undriven_4), .GND(ds1302_1_gnd));
  RotaryEncoder rotaryencoder_1 (
    .S1(undriven_10), .S2(undriven_11), .KEY(undriven_12), .Vcc(stepupmodule_1_vcc_5v),
    .GND(rotaryencoder_1_gnd));
  stepUpModule stepupmodule_1 (
    .IN_Vcc(tp4056_1_out_vcc), .IN_GND(tp4056_1_out_gnd), .Vcc_5V(stepupmodule_1_vcc_5v),
    .GND(rotaryencoder_1_gnd));  // open: D_Vcc, D_GND
endmodule

// Display
module MRB3503 (
  input  CS,
  input  RS,
  input  WR,
  input  RD,
  input  RST,
  input  DB0,
  input  DB1,
  input  DB2,
  input  DB3,
  input  DB4,
  input  DB5,
  input  DB6,
  input  DB7,
  input  DB8,
  input  DB9,
  input  DB10,
  input  DB11,
  input  DB12,
  input  DB13,
  input  DB14,
  input  DB15,
  input  SDCS,
  input  BL,
  input  Vcc_1,
  input  Vcc_2,
  input  GND_1,
  input  GND_2,
  input  Vout_5V,
  input  MISO,
  input  MOSI,
  input  PEN,
  input  F_CS,
  input  T_CS,
  input  CLK
);
endmodule

// 5V Step Up
module stepUpModule (
  input  IN_Vcc,
  input  IN_GND,
  output GND,
  output D_Vcc,
  output D_GND,
  output Vcc_5V
);
endmodule

// Charger
module TP4056 (
  input  IN_Vcc,
  input  IN_GND,
  output Out_Vcc,
  output B_Vcc,
  output B_GND,
  output Out_GND
);
endmodule

module DS1302 (
  input  Vcc,
  input  CLK,
  input  DAT,
  input  RST,
  output GND
);
endmodule

// Rotary
module RotaryEncoder (
  input  S1,
  input  S2,
  input  KEY,
  input  Vcc,
  output GND
);
endmodule

module Speaker (
  input  Vcc,
  output GND
);
endmodule

// NodeMCU v2
module NodeMCUv2 (
  input  A0,
  input  D0,
  input  RSV_1,
  input  D1,
  input  RSV_2,
  input  D2,
  input  SD3,
  input  D3,
  input  SD2,
  input  D4,
  input  SD1,
  input  Vout_3V3_2,
  input  CMD,
  input  GND_3,
  input  SD0,
  input  D5,
  input  CLK,
  input  D6,
  input  GND_1,
  input  D7,
  input  Vout_3V3_1,
  input  D8,
  input  EN,
  input  D9,
  input  RST,
  input  D10,
  input  GND_2,
  input  GND_4,
  input  Vin,
  input  Vout_3V3_3
);
endmodule

module Battery (
  input  B_in,
  output B_out
);
endmodule
